# Fritzing sketch şema.fritzibng (saved by Fritzing 0.9.10b)
breadboards: 1

parts:
  Parça1 = RFID-RC522-v3
  Parça2 = Arduino Uno (Rev3)
  Mod1 = KY-016 RGB Full Color LED Module [package="Breakout board"]
  Mod2 = MQ-7 breakout
  J3 = Piezo Speaker
  J4 = Basic Servo
  LCM1602_IIC1 = LCM1602 IIC [part_number="LCM1602 IIC" chip_label="LCM1602 IIC" package="DIP (Dual Inline) [THT]"]
  LCD1 = LCD screen
  U1 = ESP8266 WiFi Module [part_number=ESP8266]
  C1 = Capacitor Polarized [package=cpol-radial-10uf-25v]

nets:
  N1: Parça1.SDA, Parça2.D10_PWM/SS
  N2: Parça1.SCK, Parça2.D13/SCK
  N3: Parça1.MOSI, Parça2.D11_PWM/MOSI
  N4: Parça1.MISO, Parça2.D12/MISO
  GND: Parça1.GND, Parça2.GND, Mod1.-, Mod2.GND, J3.pin1, J4.gnd, LCM1602_IIC1.GND, U1.GND, C1.-
  N5: Parça1.RST, Parça2.D9_PWM
  3.3V: Parça1.3.3V, Parça2.3V3, U1.VCC, U1.RST, C1.+
  N6: Parça2.A0, Mod2.AO
  N7: Parça2.D8, J4.pulse
  N8: Parça2.A4/SDA, LCM1602_IIC1.SDA
  N9: Parça2.A5/SCL, LCM1602_IIC1.SCL
  N10: Parça2.D2, U1.TXD
  N11: Parça2.D3_PWM, U1.RXD
  N12: Parça2.D4, J3.pin2
  N13: Parça2.D5_PWM, Mod1.G
  N14: Parça2.D6_PWM, Mod1.R
  VCC: Parça2.5V, Mod2.VCC, J4.vcc, LCM1602_IIC1.VCC
  VSS: LCM1602_IIC1.VSS, LCD1.VSS
  VDD: LCM1602_IIC1.VDD, LCD1.VDD
  N15: LCM1602_IIC1.V0, LCD1.V0
  N16: LCM1602_IIC1.RS, LCD1.RS
  N17: LCM1602_IIC1.RW, LCD1.R/W
  N18: LCM1602_IIC1.E, LCD1.E
  N19: LCM1602_IIC1.D0, LCD1.DB0
  N20: LCM1602_IIC1.D1, LCD1.DB1
  N21: LCM1602_IIC1.D2, LCD1.DB2
  N22: LCM1602_IIC1.D3, LCD1.DB3
  N23: LCM1602_IIC1.D4, LCD1.DB4
  N24: LCM1602_IIC1.D5, LCD1.DB5
  N25: LCM1602_IIC1.D6, LCD1.DB6
  N26: LCM1602_IIC1.D7, LCD1.DB7
  N27: LCM1602_IIC1.A, LCD1.LED+
  N28: LCM1602_IIC1.K, LCD1.LED-
  N29: LCM1602_IIC1.LED_A, LCM1602_IIC1.LED_B

custom parts:
  RFID-RC522-v3: A simple China made RFID-RC522 Reader (6x4 cm); do check the pin labels, as this is a MFRC522 based clone.
  KY-016 RGB Full Color LED Module: KY-016 Arduino full color 5mm RGB LED, different colors can be obtained by mixing the three primary colors.
  MQ-7 breakout: MQ-5 gas sensor
  LCM1602 IIC: I2C-Module to use a 1602 or 2004 LCD on with the wire.h libory Serial LCD Modul
  ESP8266 WiFi Module: Generic WiFi Module based on the ESP8266 with onboard PCB antenna and UART communications

// code stored in the sketch: Untitled.ino
//------------------------------------------------------------------------------------kütüphanemizi  tan?mzl?yoruz------------------------------------------------------------------------------------
#include <MQ2.h> 
#include <LiquidCrystal_I2C.h>
LiquidCrystal_I2C lcd(0x3F, 16, 2);


//------------------------------------------------------------------------------------rf ?d kütüphaneleri -------------------------------------------------------------------------
#include <SPI.h>                          //iletii?im kütüphanesi
#include <MFRC522.h>                      //rf ?d kütüphanesi 
#include <Servo.h>                        //Servo kütüphanesi
//------------------------------------------------------------------------------------  pin tan?mlama rf ?d ve seervO ------------------------------------------------------------------------------------
int RST_PIN = 9;                          //rf?d?n?n reset pinini tan?t?yoruz
int SS_PIN = 10;                          //rf ?d?n?n chip select pinini tan?t?yoruz
int servoPin = 8;                         //Servo motor pinini tan?t?youz
//------------------------------------------------------------------------------------buzer pin tan?mlama
int buzzerPin = 4;                       //buzzeri tan?t?yoruz


//-----------------------------------------------------------------------------------esik de?er beliriyoruz -----------------------------------------------------------------------------------
int esikDeger = 200;                      //esik de?eri beliyliyoruz
  
//------------------------------------------------------------------------------------led pin tan?mlama ------------------------------------------------------------------------------------
int yled = 5;                            //ye?il led pini
int kled = 6;                            //k?rm?z? led pini


//------------------------------------------------------------------------------------ rf ?d de?er ?d lei ------------------------------------------------------------------------------------
Servo motor;                              //Servo motor için de?i?ken olu?turuyoruz
MFRC522 rfid(SS_PIN, RST_PIN);            //rf ?d modülü ayarlar?n? yap?yoruz.
byte ID[4] = {101,217,0,109};             //ID bilgisini giriyoruz
//------------------------------------------------------------------------------------gaz sensötü ------------------------------------------------------------------------------------
int Analog_Input = A0;                   //sensörün anolog pininw ba?lan?d?gn? tan?t?yotuz
int smoke;                               // duman? (bozulam oran?n? ölçüyoruz)
MQ2 mq2(Analog_Input);                   //sensörün anolog pininw ba?lan?d?gn? tan?t?yotuz



void setup(){


// ------------------------------------------------------------------------------------ba?lat?yoruz ------------------------------------------------------------------------------------
  Serial.begin(9600);                     // bilgi ekran?n? ba?lat?yoruz
  lcd.init();                             //lcd ekran? ba?lat?youz
  lcd.backlight();                        // lcd ekran?n arka ???g?n? balat?yoruz
  mq2.begin();                            //gaz sensörünü ba?lat?yoruz


//------------------------------------------------------------------------------------ rf ?d ba?layt?ortuz ------------------------------------------------------------------------------------
  motor.attach(servoPin);                 //Servo motor pinini motor de?i?keni ile ili?kilendiyirouz.
  Serial.begin(9600);                     //Seri haberle?meyi ba?lat?yoruz
  SPI.begin();                            //ileti?im kütüphanesimni ba?lat?yoruz
  rfid.PCD_Init();                        //rf ?d modülünü ba?lat?yoruz
//------------------------------------------------------------------------------------buzzer giri?i belirtiyoruz-----------------------------------------------------------------------------------
 
  pinMode(buzzerPin,OUTPUT);             //buzzeri çal??t?r?oyuz



//------------------------------------------------------------------------------------led giri?leri belitiroyux------------------------------------------------------------------------------------


  pinMode (yled,OUTPUT);                 //ye?il ledi ba?lat?yoruz
  pinMode (kled,OUTPUT);                 //k?rm?z? ledi ba?lat?yoruz
  
}


void loop(){


 //------------------------------------------------------------------------------------  gaz sensörünü okuyoruz ------------------------------------------------------------------------------------
  float* values= mq2.read(true);                 //gazdan gelen bilgileri okuyoruz
  smoke = mq2.readSmoke();                       //gazdan duman bilgsini al?yoeuz
//------------------------------------------------------------------------------------  buzzeri ve ledi yak?yoruz ------------------------------------------------------------------------------------ 
   int bilgi = analogRead (A0);                  //bilgi için gaz sensörünü kullan?yoruz
  if (bilgi>esikDeger) {                         //esik de?eri aarl?yoruz
    digitalWrite(buzzerPin,0);                   //buzzer pinin devre d??? b?rak?yoruz
    digitalWrite(kled,1);                        //k?rm?z? led aktifle?tiriyoruz
    digitalWrite(yled,0);                        //ye?il ledi devre d??l? br?ka?yoruz
    delay(100);                                  //1sn bekliyoru
    digitalWrite(buzzerPin,1);                  //buzzer pinin etkinl?e?tiriyoruz
    digitalWrite(kled,1);                        //k?rm?z? led aktifle?tiriyoruz
    digitalWrite(yled,0);                        //ye?il ledi devre d??? 
    delay(100);                                  //1sn bekliyoru
  } 
  else{
    digitalWrite(buzzerPin,0);                   //buzzer pinin devre d??? b?rak?yoruz                  
    digitalWrite(kled,0);                        //k?rm?z? ledi devred??? b?rka?yoruz
    digitalWrite(yled,1);                        //ye?il ledi ba?lat?y?rouz
  }
 //------------------------------------------------------------------------------------  gaz -sensörünu lcd eranda okuyoruz ------------------------------------------------------------------------------------
  lcd.clear();                                  //lcd ekran? temizliyoruz
  lcd.setCursor(1,0);                           //lcd ekran??n 2.sat?r?n 1 sütünündan yazmay? ba?l?yoruz
  lcd.print("Bozulma orani:");                   //lcd ekran??n 1.sat?r?n 1 sütününa bozulma oran? yazd?r?yoruz
  lcd.setCursor(7,1);                           //lcd ekran??n 2.sat?r?n 7 sütünündan yazmay? ba?l?yoruz
  lcd.print((smoke*100)/10000);                  //lcd ekran??n 2.sat?r?n 7 sütününa duman de?erini yaz?yoruz
  lcd.print(" %");                               //lcd ekran??n 2.sat?r?n 7 sütününa % de?eri ekliyoruz
  delay(100);                                    //0.1 saniye bekliyoruz


//---------------------------------------------------------------------------------- rf ?d nin ?d kar??la?t?rmas? -----------------------------------------------------------------------------  
  if ( ! rfid.PICC_IsNewCardPresent())     //Yeni kart?n okunmas?n? bekliyoruz
    return;


  if ( ! rfid.PICC_ReadCardSerial())      //Kart okunmad??? zaman bekliyoruz
    return;


  if (rfid.uid.uidByte[0] == ID[0] &&     //Okunan kart ID'si ile ID de?i?kenini kar??la?t?r?yoruz.
    rfid.uid.uidByte[1] == ID[1] && 
    rfid.uid.uidByte[2] == ID[2] && 
    rfid.uid.uidByte[3] == ID[3] ) {


  
 //-----------------------------------------------------------------------------  servo dödnrürüyoruz -----------------------------------------------------------------------------      
        Serial.println("Kapi acildi");      //bilgi ekra?n?a kap? aç?ld? yazd?r?yoruz
        ekranaYazdir();                    //ekrana yazd?r?y?eozu
        motor.write(180);                 //Servo motoru 180 dereceye getiriyoruz
        delay(1000);                      //1sn bekliyoruz
        motor.write(0);                   //Servo motoru 0 dereceye getiriyoru
        delay(100);                       //1msn bekliyoruz
 //-----------------------------------------------------------------------------led ekrana ba?ar?l? giri? yazd?rma --------------------------------------------------------------------------
        lcd.clear();                     //lcd ekran? temizliyoruz    
        lcd.setCursor(0,0);              //lcd ekran?n 1.sat?r 1.sütünündan yazmaya ba?l?yoruz
        lcd.print("  Motor kapagi");     //lcd ekran?n 1.sat?r 1.sütününa motor kapaa?? yaz?d?r?otuez     
        lcd.setCursor(6,1);              //lcd ekran??n 2.sat?r?n 6 sütünündan yazmay? ba?l?yoruz
        lcd.print("acik");               //lcd ekran??n 2.sat?r?n 6 sütününa  aç?k yaz?yoruz
        delay(3000);                     //3sn bekliyoruz
    }
    else{                                 //Yetkisiz giri?te içerideki komutlar çal??t?r?l?r.
      Serial.println("Yetkisiz Kart");        //bilgi ekran?n ayetksiiz yerksiiz yazd?r?yoruz
      ekranaYazdir();                        // bilgi ekran?n ayazd?r?yoruz
 //------------------------------------------------------------------------------------ yetkisiZ giri?te lcd dekranana yetkisiz gir? yazd?r?yoruz---------------------------------------------------------


      lcd.clear();                            //lcd ekran?n temizliyoruz
      lcd.setCursor(0,0);                     //lcd ekran?n 1.sat?r 1.sütünündan yazömaay ba?l?yoruz
      lcd.print(" Yetkisiz Giris");             //lcd ekran?n 1.sat?r 1.sütününa teksizi giri? yazd?r?yoruz
      delay(3000);                             //3sn bekliyoruz
   }
  rfid.PICC_HaltA();
//------------------------------------------------------------------------------------



}
//-----------------------------------------------------------------------------  serial mo?nitçe yazd?rr?yoruz ----------------------------------------------------------------------------- 
void ekranaYazdir(){                    
  Serial.print("ID Numarasi: ");                   // (?d nuamras?n? yazd?r?youz)
  for(int sayac = 0; sayac < 4; sayac++){
    Serial.print(rfid.uid.uidByte[sayac]);
    Serial.print(" ");                              // seral ekranda "" içindeki de?erleri yazsd??r?youz
  }
  Serial.println("");                                     // seral ekranda "" içindeki de?erleri yazsd??r?youz
}
